# Fritzing sketch plantwater (saved by Fritzing 0.9.4)
breadboards: 1

parts:
  Argon1 = Particle Argon
  Relay1 = Relay - 6 pins [package="DIP (Dual Inline) [THT]"]
  M1 = BMP280
  Grove1 = Grove Dust Sensor
  SENS1 = SoilWatch 10
  U1 = AQ_Sensor [package=mq-3]
  Q1 = PNP-Transistor [package="SOT-23 [SMD]"]
  R1 = Resistor [tolerance=±5% resistance=220 package="0402 [SMD]"]
  R2 = Resistor [tolerance=±5% resistance=220 package="0402 [SMD]"]
  M2 = DC Motor
  OLED_I2C1 = OLED 128x64 I2C Monochrome Display

nets:
  3.3V: Argon1.3.3V, M1.VIN, SENS1.VCC, OLED_I2C1.VDD
  GND: Argon1.GND, Relay1.GND, M1.GND, Grove1.NC, SENS1.GND, U1.NC, Q1.1, R2.Pin_0, M2.pin_2, OLED_I2C1.GND
  N1: Argon1.A0, SENS1.OUT
  N2: Argon1.A1, U1.Vcc
  N3: Argon1.A2, Grove1.VCC
  N4: Argon1.MI, Relay1.VCC, Q1.0, R2.Pin_1
  N5: Argon1.SDA, M1.SDA, OLED_I2C1.SDA
  N6: Argon1.SCL, M1.SCL, OLED_I2C1.SCK
  N7: Argon1.VUSB, Relay1.ON, Grove1.SIG, U1.Aout, R1.Pin_0
  N8: Relay1.COM, M2.pin_1
  N9: Q1.2, R1.Pin_1

custom parts:
  Particle Argon: The Argon is a powerful Wi-Fi enabled development board that can act as either a standalone Wi-Fi endpoint or Wi-Fi enabled gateway for Particle Mesh networks. It is based on the Nordic nRF52840 and has built-in battery charging circuitry so it’s easy to connect a Li-Po and deploy your local network in minutes. The Argon is great for connecting existing projects to the Particle Device Cloud or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
  Relay - 6 pins: A DIP stand-in part for whatever IC you want. With 6 pins on a 900mil dual inline package (DIP) footprint.
  BMP280: Temperature Humidity Barometric presure Sensor, I2C
  Grove Dust Sensor: PPD42 Grove Dust Sensor
  SoilWatch 10: SoilWatch 10 - Capacitive soil moisture sensor
  AQ_Sensor: MQ-3 alcohol gas sensor . FP not tested. SEN-08880.
